# Fritzing sketch led_eta_serbo_konexioak (saved by Fritzing 0.9.3b)
breadboards: 1

parts:
  LED1 = LED - 5mm [color="Red (633nm)" package="5 mm [THT]"]
  Part3 = iceZUM Alhambra
  R1 = Resistor [tolerance=±5% resistance=220 package=THT]
  R2 = Resistor [tolerance=±5% resistance=220 package=THT]
  LED2 = LED - 5mm [color="Red (633nm)" package="5 mm [THT]"]
  J1 = Basic Servo

nets:
  N1: LED1.cathode, R1.Pin_0
  N2: LED1.anode, Part3.GP0
  N3: Part3.G0, J1.gnd
  N4: Part3.V0#45, J1.vcc
  N5: Part3.V0#59, J1.pulse
  N6: Part3.GD1, Part3.GND, R1.Pin_1, R2.Pin_1
  N7: Part3.GP4, Part3.GP6, LED2.anode
  N8: R2.Pin_0, LED2.cathode

custom parts:
  iceZUM Alhambra: Arduino/zum compatible Open FPGA electronic board. Synthesize hardware easily, using only open source tools
